# Fritzing sketch ks_neo (saved by Fritzing 0.9.2b)
breadboards: 1

parts:
  Part1 = Arduino Uno (Rev3)
  LCD1 = LCD screen
  R1 = Rotary Potentiometer (Small) [maximum_resistance=100kΩ package=THT]
  J1 = Piezo Speaker
  R2 = Resistor [tolerance=±5% resistance=10k package=THT]
  S2 = Round Pushbutton

nets:
  N1: Part1.D8, LCD1.DB5
  N2: Part1.D9_PWM, LCD1.DB4
  N3: Part1.D10_PWM/SS, LCD1.E
  N4: Part1.D11_PWM/MOSI, LCD1.R/W
  N5: Part1.D12/MISO, LCD1.RS
  GND: Part1.GND, LCD1.VSS, R1.leg2, J1.pin1, R2.Pin_1
  N6: Part1.D2, Part1.3V3, R2.Pin_0, S2.leg0, S2.leg1
  N7: Part1.D3_PWM, J1.pin2
  N8: Part1.D6_PWM, LCD1.DB7
  N9: Part1.D7, LCD1.DB6
  5V: Part1.5V, LCD1.VDD, R1.leg1
  N10: LCD1.V0, R1.wiper
